# Fritzing sketch DataViz (saved by Fritzing 0.9.4)
breadboards: 1

parts:
  ZOMBIE = Arduino Uno (Rev3)
  WATER = Arduino Uno (Rev3)
  ZOMBIE_MOTOR = 28BYJ-48 Stepper Motor
  WATER_MOTOR = 28BYJ-48 Stepper Motor
  part = X113647 Stepper Driver Board [package=board]
  part_2 = X113647 Stepper Driver Board [package=board]
  GREEN = Pushbutton [package="[THT]"]
  BLUE = Pushbutton [package="[THT]"]
  RED = Pushbutton [package="[THT]"]
  RED_2 = Pushbutton [package="[THT]"]
  R1 = Resistor [tolerance=±5% resistance=10k package="0805 [SMD]"]
  R2 = Resistor [tolerance=±5% resistance=10k package="0805 [SMD]"]
  R3 = Resistor [tolerance=±5% resistance=10k package="0805 [SMD]"]
  R4 = Resistor [tolerance=±5% resistance=10k package="0805 [SMD]"]

nets:
  N1: ZOMBIE.D9_PWM, part.IN1
  N2: ZOMBIE.D10_PWM/SS, part.IN2
  N3: ZOMBIE.D11_PWM/MOSI, part.IN3
  N4: ZOMBIE.D12/MISO, part.IN4
  GND: ZOMBIE.GND, part.GND, R3.Pin_0, R4.Pin_0
  N5: ZOMBIE.D2, ZOMBIE.D4, ZOMBIE.5V, part.+V, GREEN.Pin_3, GREEN.Pin_4, RED.Pin_3, RED.Pin_4
  N6: WATER.D9_PWM, part_2.IN1
  N7: WATER.D10_PWM/SS, part_2.IN2
  N8: WATER.D11_PWM/MOSI, part_2.IN3
  N9: WATER.D12/MISO, part_2.IN4
  GND_2: WATER.GND, part_2.GND, R1.Pin_0, R2.Pin_0
  N10: WATER.D2, WATER.D4, WATER.5V, part_2.+V, BLUE.Pin_3, BLUE.Pin_4, RED_2.Pin_3, RED_2.Pin_4
  N11: ZOMBIE_MOTOR.RED, part.RED
  N12: ZOMBIE_MOTOR.ORANGE, part.ORANGE
  N13: ZOMBIE_MOTOR.YELLOW, part.YELLOW
  N14: ZOMBIE_MOTOR.PINK, part.PINK
  N15: ZOMBIE_MOTOR.BLUE, part.BLUE
  N16: WATER_MOTOR.RED, part_2.RED
  N17: WATER_MOTOR.ORANGE, part_2.ORANGE
  N18: WATER_MOTOR.YELLOW, part_2.YELLOW
  N19: WATER_MOTOR.PINK, part_2.PINK
  N20: WATER_MOTOR.BLUE, part_2.BLUE
  N21: GREEN.Pin_1, GREEN.Pin_2, R4.Pin_1
  N22: BLUE.Pin_2, R1.Pin_1
  N23: RED.Pin_2, R3.Pin_1
  N24: RED_2.Pin_1, RED_2.Pin_2, R2.Pin_1

custom parts:
  X113647 Stepper Driver Board: A common stepper motor driver board based on ULN2003APG darlington array
